# Fritzing sketch schematic (saved by Fritzing 0.8.7b)

parts:
  Nano = Arduino Nano (Rev3.0) (ICSP)
  SSD1306_OLED = OLED 128x64 I2C Monochrome Display
  Power_source_(representation) = Battery Holders [package=battery-aa-kit]
  R1 = Temperature Sensor (Thermistor) [thermistor_type=NTC package=THT]
  R2 = Temperature Sensor (Thermistor) [thermistor_type=NTC package=THT]
  R3 = Temperature Sensor (Thermistor) [thermistor_type=NTC package=THT]
  10k? = Resistor [tolerance=±5% resistance=220 package="1206 [SMD]"]
  R4 = Temperature Sensor (Thermistor) [thermistor_type=NTC package=THT]

nets:
  GND: Nano.GND, SSD1306_OLED.GND, R1.pin_1, R2.pin_1, R4.pin_1
  5V: Nano.5V, SSD1306_OLED.VDD, Power_source_(representation).-, 10k?.Pin_0
  N1: Nano.A5, SSD1306_OLED.SCK
  N2: Nano.A4, SSD1306_OLED.SDA
  N3: Nano.A3, Nano.A2, Nano.A1, Nano.A0, R1.pin_0, R2.pin_0, R3.pin_0, 10k?.Pin_1, R4.pin_0
  N4: Power_source_(representation).+, R3.pin_1
